// Logisim project CODE.circ as structural Verilog
module XOR (
  input  A,
  input  B,
  output OUT
);

  wire nand_1_out, or_1_out;

  OR or_1 (.A(A), .B(B), .OUT(or_1_out));
  NAND nand_1 (.A(A), .B(B), .OUT(nand_1_out));
  AND and_1 (.A(or_1_out), .B(nand_1_out), .OUT(OUT));
endmodule

module NOR (
  input  A,
  input  B,
  output OUT
);

  wire or_1_out;

  OR or_1 (.A(A), .B(B), .OUT(or_1_out));
  NOT not_1 (.IN(or_1_out), .OUT(OUT));
endmodule

module NAND (
  input  A,
  input  B,
  output OUT
);

  wire and_1_out;

  AND and_1 (.A(A), .B(B), .OUT(and_1_out));
  NOT not_1 (.IN(and_1_out), .OUT(OUT));
endmodule

// HADD
module HALF_ADDER (
  input  A,
  input  B,
  output SUM_OUT,
  output CARRY_OUT
);

  XOR xor_1 (.A(A), .B(B), .OUT(SUM_OUT));
  AND and_1 (.A(A), .B(B), .OUT(CARRY_OUT));
endmodule

// ADD
module FULL_ADDER (
  input  CARRY_IN,
  input  A,
  input  B,
  output SUM_OUT,
  output CARRY_OUT
);

  wire half_adder_1_carry_out, half_adder_1_sum_out, half_adder_2_carry_out;

  HALF_ADDER half_adder_1 (.A(A), .B(B), .SUM_OUT(half_adder_1_sum_out), .CARRY_OUT(half_adder_1_carry_out));
  HALF_ADDER half_adder_2 (
    .A(CARRY_IN), .B(half_adder_1_sum_out), .SUM_OUT(SUM_OUT), .CARRY_OUT(half_adder_2_carry_out));
  OR or_1 (.A(half_adder_2_carry_out), .B(half_adder_1_carry_out), .OUT(CARRY_OUT));
endmodule

// ADD
module EIGHT_BIT_ADDER (
  input  in_1,
  input  [7:0] in_2,
  input  [7:0] in_3,
  output [7:0] out_4,
  output CARRY_OUT
);

  wire full_adder_1_carry_out, full_adder_2_carry_out, full_adder_3_carry_out, full_adder_4_carry_out,
       full_adder_5_carry_out, full_adder_6_carry_out, full_adder_7_carry_out;

  FULL_ADDER full_adder_1 (
    .A(in_2[0]), .B(in_3[0]), .CARRY_IN(in_1), .CARRY_OUT(full_adder_1_carry_out), .SUM_OUT(out_4[0]));
  FULL_ADDER full_adder_2 (
    .A(in_2[1]), .B(in_3[1]), .CARRY_IN(full_adder_1_carry_out), .CARRY_OUT(full_adder_2_carry_out),
    .SUM_OUT(out_4[1]));
  FULL_ADDER full_adder_3 (
    .A(in_2[2]), .B(in_3[2]), .CARRY_IN(full_adder_2_carry_out), .CARRY_OUT(full_adder_3_carry_out),
    .SUM_OUT(out_4[2]));
  FULL_ADDER full_adder_4 (
    .A(in_2[3]), .B(in_3[3]), .CARRY_IN(full_adder_3_carry_out), .CARRY_OUT(full_adder_4_carry_out),
    .SUM_OUT(out_4[3]));
  FULL_ADDER full_adder_5 (
    .A(in_2[4]), .B(in_3[4]), .CARRY_IN(full_adder_4_carry_out), .CARRY_OUT(full_adder_5_carry_out),
    .SUM_OUT(out_4[4]));
  FULL_ADDER full_adder_6 (
    .A(in_2[5]), .B(in_3[5]), .CARRY_IN(full_adder_5_carry_out), .CARRY_OUT(full_adder_6_carry_out),
    .SUM_OUT(out_4[5]));
  FULL_ADDER full_adder_7 (
    .A(in_2[6]), .B(in_3[6]), .CARRY_IN(full_adder_6_carry_out), .CARRY_OUT(full_adder_7_carry_out),
    .SUM_OUT(out_4[6]));
  FULL_ADDER full_adder_8 (
    .A(in_2[7]), .B(in_3[7]), .CARRY_IN(full_adder_7_carry_out), .CARRY_OUT(CARRY_OUT), .SUM_OUT(out_4[7]));
endmodule

module AND (
  input  A,
  input  B,
  output OUT
);

  wire transistor_1_out;

  Transistor #(.\type ("n")) transistor_1 (.in(1'b1), .out(transistor_1_out), .gate(A));
  Transistor #(.\type ("n")) transistor_2 (.in(transistor_1_out), .out(OUT), .gate(B));
  Pull_Resistor pull_resistor_1 (.node(OUT));
endmodule

module OR (
  input  A,
  input  B,
  output OUT
);

  Transistor #(.\type ("n")) transistor_1 (.in(1'b1), .out(OUT), .gate(A));
  Transistor #(.\type ("n")) transistor_2 (.in(1'b1), .out(OUT), .gate(B));
  Pull_Resistor pull_resistor_1 (.node(OUT));
endmodule

module NOT (
  input  IN,
  output OUT
);

  Transistor #(.\type ("n")) transistor_1 (.in(1'b0), .out(OUT), .gate(IN));
  Pull_Resistor #(.pull(1)) pull_resistor_1 (.node(OUT));
endmodule

// OC
module EIGHT_BIT_ONES_COMPLEMENT (
  input  [7:0] IN,
  input  INVERT,
  output [7:0] OUT
);

  XOR xor_1 (.A(IN[0]), .B(INVERT), .OUT(OUT[0]));
  XOR xor_2 (.A(IN[1]), .B(INVERT), .OUT(OUT[1]));
  XOR xor_3 (.A(IN[2]), .B(INVERT), .OUT(OUT[2]));
  XOR xor_4 (.A(IN[3]), .B(INVERT), .OUT(OUT[3]));
  XOR xor_5 (.A(IN[4]), .B(INVERT), .OUT(OUT[4]));
  XOR xor_6 (.A(IN[5]), .B(INVERT), .OUT(OUT[5]));
  XOR xor_7 (.A(IN[6]), .B(INVERT), .OUT(OUT[6]));
  XOR xor_8 (.A(IN[7]), .B(INVERT), .OUT(OUT[7]));
endmodule

module EIGHT_BIT_ADDER_SUBTRACTOR (
  input  SUBTRACTION,
  input  [7:0] A,
  input  [7:0] B,
  output [7:0] OUT,
  output UNDERFLOW_OVERFLOW
);

  wire eight_bit_adder_1_carry_out;
  wire [7:0] eight_bit_ones_complement_1_out;

  EIGHT_BIT_ONES_COMPLEMENT eight_bit_ones_complement_1 (
    .IN(A), .INVERT(SUBTRACTION), .OUT(eight_bit_ones_complement_1_out));
  EIGHT_BIT_ADDER eight_bit_adder_1 (
    .in_2(eight_bit_ones_complement_1_out), .in_3(B), .in_1(SUBTRACTION),
    .CARRY_OUT(eight_bit_adder_1_carry_out), .out_4(OUT));
  XOR xor_1 (.A(eight_bit_adder_1_carry_out), .B(SUBTRACTION), .OUT(UNDERFLOW_OVERFLOW));
endmodule

// RSFF
module R_S_FLIP_FLOP (
  input  R,
  input  S,
  output Q,
  output Q_BAR
);

  NOR nor_1 (.A(R), .B(Q_BAR), .OUT(Q));
  NOR nor_2 (.A(Q), .B(S), .OUT(Q_BAR));
endmodule

// DFF
module LEVEL_TRIGGERED_D_TYPE_FLIP_FLOP (
  input  DATA,
  input  CLOCK,
  output CLOCK_OUT,
  output Q,
  output Q_BAR
);

  wire and_1_out, and_2_out, not_1_out;

  NOT not_1 (.IN(DATA), .OUT(not_1_out));
  AND and_1 (.A(not_1_out), .B(CLOCK), .OUT(and_1_out));
  AND and_2 (.A(CLOCK), .B(DATA), .OUT(and_2_out));
  R_S_FLIP_FLOP r_s_flip_flop_1 (.R(and_1_out), .S(and_2_out), .Q(Q), .Q_BAR(Q_BAR));

  assign CLOCK_OUT = CLOCK;
endmodule

// S
module EIGHT_BIT_LATCH (
  input  [7:0] DATA,
  input  CLOCK,
  output [7:0] Q
);

  wire level_triggered_d_type_flip_flop_2_clock_out, level_triggered_d_type_flip_flop_3_clock_out,
       level_triggered_d_type_flip_flop_4_clock_out, level_triggered_d_type_flip_flop_5_clock_out,
       level_triggered_d_type_flip_flop_6_clock_out, level_triggered_d_type_flip_flop_7_clock_out,
       level_triggered_d_type_flip_flop_8_clock_out;

  LEVEL_TRIGGERED_D_TYPE_FLIP_FLOP level_triggered_d_type_flip_flop_1 (
    .DATA(DATA[0]), .CLOCK(level_triggered_d_type_flip_flop_2_clock_out), .Q(Q[0]));  // open: CLOCK_OUT, Q_BAR
  LEVEL_TRIGGERED_D_TYPE_FLIP_FLOP level_triggered_d_type_flip_flop_2 (
    .DATA(DATA[1]), .CLOCK_OUT(level_triggered_d_type_flip_flop_2_clock_out),
    .CLOCK(level_triggered_d_type_flip_flop_3_clock_out), .Q(Q[1]));  // open: Q_BAR
  LEVEL_TRIGGERED_D_TYPE_FLIP_FLOP level_triggered_d_type_flip_flop_3 (
    .DATA(DATA[2]), .CLOCK_OUT(level_triggered_d_type_flip_flop_3_clock_out),
    .CLOCK(level_triggered_d_type_flip_flop_4_clock_out), .Q(Q[2]));  // open: Q_BAR
  LEVEL_TRIGGERED_D_TYPE_FLIP_FLOP level_triggered_d_type_flip_flop_4 (
    .DATA(DATA[3]), .CLOCK_OUT(level_triggered_d_type_flip_flop_4_clock_out),
    .CLOCK(level_triggered_d_type_flip_flop_5_clock_out), .Q(Q[3]));  // open: Q_BAR
  LEVEL_TRIGGERED_D_TYPE_FLIP_FLOP level_triggered_d_type_flip_flop_5 (
    .DATA(DATA[4]), .CLOCK_OUT(level_triggered_d_type_flip_flop_5_clock_out),
    .CLOCK(level_triggered_d_type_flip_flop_6_clock_out), .Q(Q[4]));  // open: Q_BAR
  LEVEL_TRIGGERED_D_TYPE_FLIP_FLOP level_triggered_d_type_flip_flop_6 (
    .DATA(DATA[5]), .CLOCK_OUT(level_triggered_d_type_flip_flop_6_clock_out),
    .CLOCK(level_triggered_d_type_flip_flop_7_clock_out), .Q(Q[5]));  // open: Q_BAR
  LEVEL_TRIGGERED_D_TYPE_FLIP_FLOP level_triggered_d_type_flip_flop_7 (
    .DATA(DATA[6]), .CLOCK_OUT(level_triggered_d_type_flip_flop_7_clock_out),
    .CLOCK(level_triggered_d_type_flip_flop_8_clock_out), .Q(Q[6]));  // open: Q_BAR
  LEVEL_TRIGGERED_D_TYPE_FLIP_FLOP level_triggered_d_type_flip_flop_8 (
    .DATA(DATA[7]), .CLOCK_OUT(level_triggered_d_type_flip_flop_8_clock_out), .CLOCK(CLOCK), .Q(Q[7]));  // open: Q_BAR
endmodule

// S
module TWO_LINE_TO_ONE_SELECTOR (
  input  SELECT,
  input  A,
  input  B,
  output OUT,
  output SELECT_OUT
);

  wire and_1_out, and_2_out, not_1_out;

  NOT not_1 (.IN(SELECT), .OUT(not_1_out));
  AND and_1 (.A(A), .B(SELECT), .OUT(and_1_out));
  AND and_2 (.A(B), .B(not_1_out), .OUT(and_2_out));
  OR or_1 (.A(and_1_out), .B(and_2_out), .OUT(OUT));

  assign SELECT_OUT = SELECT;
endmodule

module EIGHT_BIT_TWO_LINE_TO_ONE_SELECTOR (
  input  SELECT,
  input  [7:0] A,
  input  [7:0] B,
  output [7:0] OUT
);

  wire two_line_to_one_selector_1_select_out, two_line_to_one_selector_2_select_out,
       two_line_to_one_selector_3_select_out, two_line_to_one_selector_4_select_out,
       two_line_to_one_selector_5_select_out, two_line_to_one_selector_6_select_out,
       two_line_to_one_selector_7_select_out;

  TWO_LINE_TO_ONE_SELECTOR two_line_to_one_selector_1 (
    .A(A[0]), .B(B[0]), .SELECT(SELECT), .SELECT_OUT(two_line_to_one_selector_1_select_out), .OUT(OUT[0]));
  TWO_LINE_TO_ONE_SELECTOR two_line_to_one_selector_2 (
    .A(A[1]), .B(B[1]), .SELECT(two_line_to_one_selector_1_select_out),
    .SELECT_OUT(two_line_to_one_selector_2_select_out), .OUT(OUT[1]));
  TWO_LINE_TO_ONE_SELECTOR two_line_to_one_selector_3 (
    .A(A[2]), .B(B[2]), .SELECT(two_line_to_one_selector_2_select_out),
    .SELECT_OUT(two_line_to_one_selector_3_select_out), .OUT(OUT[2]));
  TWO_LINE_TO_ONE_SELECTOR two_line_to_one_selector_4 (
    .A(A[3]), .B(B[3]), .SELECT(two_line_to_one_selector_3_select_out),
    .SELECT_OUT(two_line_to_one_selector_4_select_out), .OUT(OUT[3]));
  TWO_LINE_TO_ONE_SELECTOR two_line_to_one_selector_5 (
    .A(A[4]), .B(B[4]), .SELECT(two_line_to_one_selector_4_select_out),
    .SELECT_OUT(two_line_to_one_selector_5_select_out), .OUT(OUT[4]));
  TWO_LINE_TO_ONE_SELECTOR two_line_to_one_selector_6 (
    .A(A[5]), .B(B[5]), .SELECT(two_line_to_one_selector_5_select_out),
    .SELECT_OUT(two_line_to_one_selector_6_select_out), .OUT(OUT[5]));
  TWO_LINE_TO_ONE_SELECTOR two_line_to_one_selector_7 (
    .A(A[6]), .B(B[6]), .SELECT(two_line_to_one_selector_6_select_out),
    .SELECT_OUT(two_line_to_one_selector_7_select_out), .OUT(OUT[6]));
  TWO_LINE_TO_ONE_SELECTOR two_line_to_one_selector_8 (
    .A(A[7]), .B(B[7]), .SELECT(two_line_to_one_selector_7_select_out), .OUT(OUT[7]));  // open: SELECT_OUT
endmodule

// DFF
module LEVEL_TRIGGERED_D_TYPE_FLIP_FLOP_WITH_CLEAR (
  input  CLEAR,
  input  DATA,
  input  CLOCK,
  output CLOCK_OUT,
  output Q,
  output Q_BAR,
  output CLEAR_OUT
);

  wire and_1_out, and_2_out, not_1_out, or_1_out;

  NOT not_1 (.IN(DATA), .OUT(not_1_out));
  AND and_1 (.A(not_1_out), .B(CLOCK), .OUT(and_1_out));
  AND and_2 (.A(CLOCK), .B(DATA), .OUT(and_2_out));
  OR or_1 (.A(CLEAR), .B(and_1_out), .OUT(or_1_out));
  R_S_FLIP_FLOP r_s_flip_flop_1 (.R(or_1_out), .S(and_2_out), .Q(Q), .Q_BAR(Q_BAR));

  assign CLEAR_OUT = CLEAR;
  assign CLOCK_OUT = CLOCK;
endmodule

module EIGHT_BIT_LATCH_WITH_CLEAR (
  input  CLEAR,
  input  [7:0] IN,
  input  CLOCK,
  output [7:0] OUT
);

  wire level_triggered_d_type_flip_flop_with_clear_1_clear_out,
       level_triggered_d_type_flip_flop_with_clear_2_clear_out,
       level_triggered_d_type_flip_flop_with_clear_2_clock_out,
       level_triggered_d_type_flip_flop_with_clear_3_clear_out,
       level_triggered_d_type_flip_flop_with_clear_3_clock_out,
       level_triggered_d_type_flip_flop_with_clear_4_clear_out,
       level_triggered_d_type_flip_flop_with_clear_4_clock_out,
       level_triggered_d_type_flip_flop_with_clear_5_clear_out,
       level_triggered_d_type_flip_flop_with_clear_5_clock_out,
       level_triggered_d_type_flip_flop_with_clear_6_clear_out,
       level_triggered_d_type_flip_flop_with_clear_6_clock_out,
       level_triggered_d_type_flip_flop_with_clear_7_clear_out,
       level_triggered_d_type_flip_flop_with_clear_7_clock_out,
       level_triggered_d_type_flip_flop_with_clear_8_clock_out;

  LEVEL_TRIGGERED_D_TYPE_FLIP_FLOP_WITH_CLEAR level_triggered_d_type_flip_flop_with_clear_1 (
    .DATA(IN[0]), .CLEAR(CLEAR), .CLOCK(level_triggered_d_type_flip_flop_with_clear_2_clock_out),
    .CLEAR_OUT(level_triggered_d_type_flip_flop_with_clear_1_clear_out), .Q(OUT[0]));  // open: CLOCK_OUT, Q_BAR
  LEVEL_TRIGGERED_D_TYPE_FLIP_FLOP_WITH_CLEAR level_triggered_d_type_flip_flop_with_clear_2 (
    .DATA(IN[1]), .CLOCK_OUT(level_triggered_d_type_flip_flop_with_clear_2_clock_out),
    .CLEAR(level_triggered_d_type_flip_flop_with_clear_1_clear_out),
    .CLOCK(level_triggered_d_type_flip_flop_with_clear_3_clock_out),
    .CLEAR_OUT(level_triggered_d_type_flip_flop_with_clear_2_clear_out), .Q(OUT[1]));  // open: Q_BAR
  LEVEL_TRIGGERED_D_TYPE_FLIP_FLOP_WITH_CLEAR level_triggered_d_type_flip_flop_with_clear_3 (
    .DATA(IN[2]), .CLOCK_OUT(level_triggered_d_type_flip_flop_with_clear_3_clock_out),
    .CLEAR(level_triggered_d_type_flip_flop_with_clear_2_clear_out),
    .CLOCK(level_triggered_d_type_flip_flop_with_clear_4_clock_out),
    .CLEAR_OUT(level_triggered_d_type_flip_flop_with_clear_3_clear_out), .Q(OUT[2]));  // open: Q_BAR
  LEVEL_TRIGGERED_D_TYPE_FLIP_FLOP_WITH_CLEAR level_triggered_d_type_flip_flop_with_clear_4 (
    .DATA(IN[3]), .CLOCK_OUT(level_triggered_d_type_flip_flop_with_clear_4_clock_out),
    .CLEAR(level_triggered_d_type_flip_flop_with_clear_3_clear_out),
    .CLOCK(level_triggered_d_type_flip_flop_with_clear_5_clock_out),
    .CLEAR_OUT(level_triggered_d_type_flip_flop_with_clear_4_clear_out), .Q(OUT[3]));  // open: Q_BAR
  LEVEL_TRIGGERED_D_TYPE_FLIP_FLOP_WITH_CLEAR level_triggered_d_type_flip_flop_with_clear_5 (
    .DATA(IN[4]), .CLOCK_OUT(level_triggered_d_type_flip_flop_with_clear_5_clock_out),
    .CLEAR(level_triggered_d_type_flip_flop_with_clear_4_clear_out),
    .CLOCK(level_triggered_d_type_flip_flop_with_clear_6_clock_out),
    .CLEAR_OUT(level_triggered_d_type_flip_flop_with_clear_5_clear_out), .Q(OUT[4]));  // open: Q_BAR
  LEVEL_TRIGGERED_D_TYPE_FLIP_FLOP_WITH_CLEAR level_triggered_d_type_flip_flop_with_clear_6 (
    .DATA(IN[5]), .CLOCK_OUT(level_triggered_d_type_flip_flop_with_clear_6_clock_out),
    .CLEAR(level_triggered_d_type_flip_flop_with_clear_5_clear_out),
    .CLOCK(level_triggered_d_type_flip_flop_with_clear_7_clock_out),
    .CLEAR_OUT(level_triggered_d_type_flip_flop_with_clear_6_clear_out), .Q(OUT[5]));  // open: Q_BAR
  LEVEL_TRIGGERED_D_TYPE_FLIP_FLOP_WITH_CLEAR level_triggered_d_type_flip_flop_with_clear_7 (
    .DATA(IN[6]), .CLOCK_OUT(level_triggered_d_type_flip_flop_with_clear_7_clock_out),
    .CLEAR(level_triggered_d_type_flip_flop_with_clear_6_clear_out),
    .CLOCK(level_triggered_d_type_flip_flop_with_clear_8_clock_out),
    .CLEAR_OUT(level_triggered_d_type_flip_flop_with_clear_7_clear_out), .Q(OUT[6]));  // open: Q_BAR
  LEVEL_TRIGGERED_D_TYPE_FLIP_FLOP_WITH_CLEAR level_triggered_d_type_flip_flop_with_clear_8 (
    .DATA(IN[7]), .CLOCK_OUT(level_triggered_d_type_flip_flop_with_clear_8_clock_out),
    .CLEAR(level_triggered_d_type_flip_flop_with_clear_7_clear_out), .CLOCK(CLOCK), .Q(OUT[7]));  // open: CLEAR_OUT, Q_BAR
endmodule

// DFF
module EDGE_TRIGGERED_D_TYPE_FLIP_FLOP (
  input  INITIALIZE,
  input  DATA,
  input  CLOCK,
  output CLOCK_OUT,
  output Q,
  output Q_BAR,
  output INITIALIZE_OUT
);

  wire and_1_out, and_2_out, and_3_out, and_4_out, not_1_out, not_2_out, or_1_out, r_s_flip_flop_1_q,
       r_s_flip_flop_1_q_bar;

  NOT not_1 (.IN(CLOCK), .OUT(not_1_out));
  NOT not_2 (.IN(DATA), .OUT(not_2_out));
  AND and_1 (.A(DATA), .B(not_1_out), .OUT(and_1_out));
  AND and_2 (.A(not_1_out), .B(not_2_out), .OUT(and_2_out));
  R_S_FLIP_FLOP r_s_flip_flop_1 (.R(and_1_out), .S(and_2_out), .Q(r_s_flip_flop_1_q), .Q_BAR(r_s_flip_flop_1_q_bar));
  AND and_3 (.A(r_s_flip_flop_1_q), .B(CLOCK), .OUT(and_3_out));
  AND and_4 (.A(CLOCK), .B(r_s_flip_flop_1_q_bar), .OUT(and_4_out));
  OR or_1 (.A(INITIALIZE), .B(and_3_out), .OUT(or_1_out));
  R_S_FLIP_FLOP r_s_flip_flop_2 (.R(or_1_out), .S(and_4_out), .Q(Q), .Q_BAR(Q_BAR));

  assign CLOCK_OUT = CLOCK;
  assign INITIALIZE_OUT = INITIALIZE;
endmodule

module EIGHT_BIT_RIPPLE_COUNTER (
  input  [7:0] TICK_GUARD,
  input  INITIALIZE,
  input  CLOCK,
  output [7:0] OUT
);

  wire edge_triggered_d_type_flip_flop_1_q_bar, edge_triggered_d_type_flip_flop_2_q_bar,
       edge_triggered_d_type_flip_flop_3_q_bar, edge_triggered_d_type_flip_flop_4_q_bar,
       edge_triggered_d_type_flip_flop_5_q_bar, edge_triggered_d_type_flip_flop_6_q_bar,
       edge_triggered_d_type_flip_flop_7_q_bar, edge_triggered_d_type_flip_flop_8_q_bar,
       two_line_to_one_selector_1_out, two_line_to_one_selector_2_out, two_line_to_one_selector_3_out,
       two_line_to_one_selector_4_out, two_line_to_one_selector_5_out, two_line_to_one_selector_6_out,
       two_line_to_one_selector_7_out, two_line_to_one_selector_8_out;

  EDGE_TRIGGERED_D_TYPE_FLIP_FLOP edge_triggered_d_type_flip_flop_1 (
    .DATA(two_line_to_one_selector_1_out), .INITIALIZE(INITIALIZE), .CLOCK(CLOCK), .Q(OUT[0]),
    .Q_BAR(edge_triggered_d_type_flip_flop_1_q_bar));  // open: CLOCK_OUT, INITIALIZE_OUT
  TWO_LINE_TO_ONE_SELECTOR two_line_to_one_selector_1 (
    .A(edge_triggered_d_type_flip_flop_1_q_bar), .B(1'b0), .SELECT(TICK_GUARD[7]),
    .OUT(two_line_to_one_selector_1_out));  // open: SELECT_OUT
  EDGE_TRIGGERED_D_TYPE_FLIP_FLOP edge_triggered_d_type_flip_flop_2 (
    .DATA(two_line_to_one_selector_2_out), .INITIALIZE(INITIALIZE), .CLOCK(two_line_to_one_selector_1_out),
    .Q(OUT[1]), .Q_BAR(edge_triggered_d_type_flip_flop_2_q_bar));  // open: CLOCK_OUT, INITIALIZE_OUT
  TWO_LINE_TO_ONE_SELECTOR two_line_to_one_selector_2 (
    .A(edge_triggered_d_type_flip_flop_2_q_bar), .B(1'b0), .SELECT(TICK_GUARD[6]),
    .OUT(two_line_to_one_selector_2_out));  // open: SELECT_OUT
  EDGE_TRIGGERED_D_TYPE_FLIP_FLOP edge_triggered_d_type_flip_flop_3 (
    .DATA(two_line_to_one_selector_3_out), .INITIALIZE(INITIALIZE), .CLOCK(two_line_to_one_selector_2_out),
    .Q(OUT[2]), .Q_BAR(edge_triggered_d_type_flip_flop_3_q_bar));  // open: CLOCK_OUT, INITIALIZE_OUT
  TWO_LINE_TO_ONE_SELECTOR two_line_to_one_selector_3 (
    .A(edge_triggered_d_type_flip_flop_3_q_bar), .B(1'b0), .SELECT(TICK_GUARD[5]),
    .OUT(two_line_to_one_selector_3_out));  // open: SELECT_OUT
  EDGE_TRIGGERED_D_TYPE_FLIP_FLOP edge_triggered_d_type_flip_flop_4 (
    .DATA(two_line_to_one_selector_4_out), .INITIALIZE(INITIALIZE), .CLOCK(two_line_to_one_selector_3_out),
    .Q(OUT[3]), .Q_BAR(edge_triggered_d_type_flip_flop_4_q_bar));  // open: CLOCK_OUT, INITIALIZE_OUT
  TWO_LINE_TO_ONE_SELECTOR two_line_to_one_selector_4 (
    .A(edge_triggered_d_type_flip_flop_4_q_bar), .B(1'b0), .SELECT(TICK_GUARD[4]),
    .OUT(two_line_to_one_selector_4_out));  // open: SELECT_OUT
  EDGE_TRIGGERED_D_TYPE_FLIP_FLOP edge_triggered_d_type_flip_flop_5 (
    .DATA(two_line_to_one_selector_5_out), .INITIALIZE(INITIALIZE), .CLOCK(two_line_to_one_selector_4_out),
    .Q(OUT[4]), .Q_BAR(edge_triggered_d_type_flip_flop_5_q_bar));  // open: CLOCK_OUT, INITIALIZE_OUT
  TWO_LINE_TO_ONE_SELECTOR two_line_to_one_selector_5 (
    .A(edge_triggered_d_type_flip_flop_5_q_bar), .B(1'b0), .SELECT(TICK_GUARD[3]),
    .OUT(two_line_to_one_selector_5_out));  // open: SELECT_OUT
  EDGE_TRIGGERED_D_TYPE_FLIP_FLOP edge_triggered_d_type_flip_flop_6 (
    .DATA(two_line_to_one_selector_6_out), .INITIALIZE(INITIALIZE), .CLOCK(two_line_to_one_selector_5_out),
    .Q(OUT[5]), .Q_BAR(edge_triggered_d_type_flip_flop_6_q_bar));  // open: CLOCK_OUT, INITIALIZE_OUT
  TWO_LINE_TO_ONE_SELECTOR two_line_to_one_selector_6 (
    .A(edge_triggered_d_type_flip_flop_6_q_bar), .B(1'b0), .SELECT(TICK_GUARD[2]),
    .OUT(two_line_to_one_selector_6_out));  // open: SELECT_OUT
  EDGE_TRIGGERED_D_TYPE_FLIP_FLOP edge_triggered_d_type_flip_flop_7 (
    .DATA(two_line_to_one_selector_7_out), .INITIALIZE(INITIALIZE), .CLOCK(two_line_to_one_selector_6_out),
    .Q(OUT[6]), .Q_BAR(edge_triggered_d_type_flip_flop_7_q_bar));  // open: CLOCK_OUT, INITIALIZE_OUT
  TWO_LINE_TO_ONE_SELECTOR two_line_to_one_selector_7 (
    .A(edge_triggered_d_type_flip_flop_7_q_bar), .B(1'b0), .SELECT(TICK_GUARD[1]),
    .OUT(two_line_to_one_selector_7_out));  // open: SELECT_OUT
  EDGE_TRIGGERED_D_TYPE_FLIP_FLOP edge_triggered_d_type_flip_flop_8 (
    .DATA(two_line_to_one_selector_8_out), .INITIALIZE(INITIALIZE), .CLOCK(two_line_to_one_selector_7_out),
    .Q(OUT[7]), .Q_BAR(edge_triggered_d_type_flip_flop_8_q_bar));  // open: CLOCK_OUT, INITIALIZE_OUT
  TWO_LINE_TO_ONE_SELECTOR two_line_to_one_selector_8 (
    .A(edge_triggered_d_type_flip_flop_8_q_bar), .B(1'b0), .SELECT(TICK_GUARD[0]),
    .OUT(two_line_to_one_selector_8_out));  // open: SELECT_OUT
endmodule

module EDGE_TRIGGERED_D_TYPE_FLIP_FLOP_WITH_PRESET_AND_CLEAR (
  input  CLEAR,
  input  PRESET,
  input  CLOCK,
  input  DATA,
  output Q,
  output Q_BAR
);

  wire not_1_out, three_input_nor_1_out, three_input_nor_2_out, three_input_nor_3_out, three_input_nor_4_out;

  NOT not_1 (.IN(CLOCK), .OUT(not_1_out));
  THREE_INPUT_NOR three_input_nor_1 (
    .A(CLEAR), .B(three_input_nor_4_out), .C(three_input_nor_2_out), .OUT(three_input_nor_1_out));
  THREE_INPUT_NOR three_input_nor_2 (.A(three_input_nor_1_out), .B(PRESET), .C(not_1_out), .OUT(three_input_nor_2_out));
  THREE_INPUT_NOR three_input_nor_3 (
    .A(three_input_nor_2_out), .B(not_1_out), .C(three_input_nor_4_out), .OUT(three_input_nor_3_out));
  THREE_INPUT_NOR three_input_nor_4 (.A(three_input_nor_3_out), .B(PRESET), .C(DATA), .OUT(three_input_nor_4_out));
  THREE_INPUT_NOR three_input_nor_5 (.A(CLEAR), .B(three_input_nor_2_out), .C(Q_BAR), .OUT(Q));
  THREE_INPUT_NOR three_input_nor_6 (.A(Q), .B(PRESET), .C(three_input_nor_3_out), .OUT(Q_BAR));
endmodule

// NOR
module THREE_INPUT_NOR (
  input  A,
  input  B,
  input  C,
  output OUT
);

  wire three_input_or_1_out;

  THREE_INPUT_OR three_input_or_1 (.A(A), .B(B), .C(C), .OUT(three_input_or_1_out));
  NOT not_1 (.IN(three_input_or_1_out), .OUT(OUT));
endmodule

// OR
module THREE_INPUT_OR (
  input  A,
  input  B,
  input  C,
  output OUT
);

  Transistor #(.\type ("n")) transistor_1 (.in(1'b1), .out(OUT), .gate(A));
  Transistor #(.\type ("n")) transistor_2 (.in(1'b1), .out(OUT), .gate(B));
  Transistor #(.\type ("n")) transistor_3 (.in(1'b1), .out(OUT), .gate(C));
  Pull_Resistor pull_resistor_1 (.node(OUT));
endmodule

// S
module EIGHT_LINE_TO_ONE_SELECTOR (
  input  [7:0] DATA,
  input  [2:0] SELECTOR,
  output OUT
);

  wire four_input_and_1_out, four_input_and_2_out, four_input_and_3_out, four_input_and_4_out,
       four_input_and_5_out, four_input_and_6_out, four_input_and_7_out, four_input_and_8_out, not_1_out,
       not_2_out, not_3_out;

  NOT not_1 (.IN(SELECTOR[0]), .OUT(not_1_out));
  NOT not_2 (.IN(SELECTOR[1]), .OUT(not_2_out));
  NOT not_3 (.IN(SELECTOR[2]), .OUT(not_3_out));
  FOUR_INPUT_AND four_input_and_1 (
    .A(DATA[0]), .B(not_1_out), .C(not_2_out), .D(not_3_out), .OUT(four_input_and_1_out));
  FOUR_INPUT_AND four_input_and_2 (
    .A(DATA[1]), .B(SELECTOR[0]), .C(not_2_out), .D(not_3_out), .OUT(four_input_and_2_out));
  FOUR_INPUT_AND four_input_and_3 (
    .A(DATA[2]), .B(SELECTOR[1]), .C(not_1_out), .D(not_3_out), .OUT(four_input_and_3_out));
  FOUR_INPUT_AND four_input_and_4 (
    .A(DATA[3]), .B(SELECTOR[0]), .C(SELECTOR[1]), .D(not_3_out), .OUT(four_input_and_4_out));
  FOUR_INPUT_AND four_input_and_5 (
    .A(DATA[4]), .B(SELECTOR[2]), .C(not_1_out), .D(not_2_out), .OUT(four_input_and_5_out));
  FOUR_INPUT_AND four_input_and_6 (
    .A(DATA[5]), .B(SELECTOR[0]), .C(SELECTOR[2]), .D(not_2_out), .OUT(four_input_and_6_out));
  FOUR_INPUT_AND four_input_and_7 (
    .A(DATA[6]), .B(SELECTOR[1]), .C(SELECTOR[2]), .D(not_1_out), .OUT(four_input_and_7_out));
  FOUR_INPUT_AND four_input_and_8 (
    .A(DATA[7]), .B(SELECTOR[0]), .C(SELECTOR[1]), .D(SELECTOR[2]), .OUT(four_input_and_8_out));
  EIGHT_INPUT_OR eight_input_or_1 (
    .A(four_input_and_1_out), .B(four_input_and_2_out), .C(four_input_and_3_out), .D(four_input_and_4_out),
    .E(four_input_and_5_out), .F(four_input_and_6_out), .G(four_input_and_7_out), .H(four_input_and_8_out),
    .OUT(OUT));
endmodule

// AND
module FOUR_INPUT_AND (
  input  A,
  input  B,
  input  C,
  input  D,
  output OUT
);

  wire transistor_1_out, transistor_2_out, transistor_3_out;

  Transistor #(.\type ("n")) transistor_1 (.in(1'b1), .out(transistor_1_out), .gate(A));
  Transistor #(.\type ("n")) transistor_2 (.in(transistor_1_out), .out(transistor_2_out), .gate(B));
  Transistor #(.\type ("n")) transistor_3 (.in(transistor_2_out), .out(transistor_3_out), .gate(C));
  Transistor #(.\type ("n")) transistor_4 (.in(transistor_3_out), .out(OUT), .gate(D));
  Pull_Resistor pull_resistor_1 (.node(OUT));
endmodule

// OR
module EIGHT_INPUT_OR (
  input  A,
  input  B,
  input  C,
  input  D,
  input  E,
  input  F,
  input  G,
  input  H,
  output OUT
);

  Transistor #(.\type ("n")) transistor_1 (.in(1'b1), .out(OUT), .gate(A));
  Transistor #(.\type ("n")) transistor_2 (.in(1'b1), .out(OUT), .gate(B));
  Transistor #(.\type ("n")) transistor_3 (.in(1'b1), .out(OUT), .gate(C));
  Transistor #(.\type ("n")) transistor_4 (.in(1'b1), .out(OUT), .gate(D));
  Transistor #(.\type ("n")) transistor_5 (.in(1'b1), .out(OUT), .gate(E));
  Transistor #(.\type ("n")) transistor_6 (.in(1'b1), .out(OUT), .gate(F));
  Transistor #(.\type ("n")) transistor_7 (.in(1'b1), .out(OUT), .gate(G));
  Transistor #(.\type ("n")) transistor_8 (.in(1'b1), .out(OUT), .gate(H));
  Pull_Resistor pull_resistor_1 (.node(OUT));
endmodule

// D
module THREE_LINE_TO_EIGHT_DECODER (
  input  DATA,
  input  [2:0] SELECTOR,
  output [7:0] OUT
);

  wire not_1_out, not_2_out, not_3_out;

  NOT not_1 (.IN(SELECTOR[0]), .OUT(not_1_out));
  NOT not_2 (.IN(SELECTOR[1]), .OUT(not_2_out));
  NOT not_3 (.IN(SELECTOR[2]), .OUT(not_3_out));
  FOUR_INPUT_AND four_input_and_1 (.A(DATA), .B(not_1_out), .C(not_2_out), .D(not_3_out), .OUT(OUT[0]));
  FOUR_INPUT_AND four_input_and_2 (.A(DATA), .B(SELECTOR[0]), .C(not_2_out), .D(not_3_out), .OUT(OUT[1]));
  FOUR_INPUT_AND four_input_and_3 (.A(DATA), .B(SELECTOR[1]), .C(not_1_out), .D(not_3_out), .OUT(OUT[2]));
  FOUR_INPUT_AND four_input_and_4 (.A(DATA), .B(SELECTOR[0]), .C(SELECTOR[1]), .D(not_3_out), .OUT(OUT[3]));
  FOUR_INPUT_AND four_input_and_5 (.A(DATA), .B(SELECTOR[2]), .C(not_1_out), .D(not_2_out), .OUT(OUT[4]));
  FOUR_INPUT_AND four_input_and_6 (.A(DATA), .B(SELECTOR[0]), .C(SELECTOR[2]), .D(not_2_out), .OUT(OUT[5]));
  FOUR_INPUT_AND four_input_and_7 (.A(DATA), .B(SELECTOR[1]), .C(SELECTOR[2]), .D(not_1_out), .OUT(OUT[6]));
  FOUR_INPUT_AND four_input_and_8 (.A(DATA), .B(SELECTOR[0]), .C(SELECTOR[1]), .D(SELECTOR[2]), .OUT(OUT[7]));
endmodule

// RAM
module EIGHT_BY_ONE_RAM (
  input  DATA,
  input  WRITE,
  input  [2:0] ADDRESS,
  input  INITIALIZE,
  output INITIALIZE_OUT,
  output OUT
);

  wire [7:0] eight_bit_initializer_1_out, level_triggered_d_type_flip_flop_1_q,
       three_line_to_eight_decoder_1_out;

  EIGHT_BIT_INITIALIZER eight_bit_initializer_1 (
    .A(three_line_to_eight_decoder_1_out), .INITIALIZE_OUT(INITIALIZE_OUT), .INITIALIZE(INITIALIZE),
    .OUT(eight_bit_initializer_1_out));
  THREE_LINE_TO_EIGHT_DECODER three_line_to_eight_decoder_1 (
    .DATA(WRITE), .SELECTOR(ADDRESS), .OUT(three_line_to_eight_decoder_1_out));
  LEVEL_TRIGGERED_D_TYPE_FLIP_FLOP level_triggered_d_type_flip_flop_1 (
    .DATA(DATA), .CLOCK(eight_bit_initializer_1_out[0]), .Q(level_triggered_d_type_flip_flop_1_q[0]));  // open: CLOCK_OUT, Q_BAR
  LEVEL_TRIGGERED_D_TYPE_FLIP_FLOP level_triggered_d_type_flip_flop_2 (
    .DATA(DATA), .CLOCK(eight_bit_initializer_1_out[1]), .Q(level_triggered_d_type_flip_flop_1_q[1]));  // open: CLOCK_OUT, Q_BAR
  LEVEL_TRIGGERED_D_TYPE_FLIP_FLOP level_triggered_d_type_flip_flop_3 (
    .DATA(DATA), .CLOCK(eight_bit_initializer_1_out[2]), .Q(level_triggered_d_type_flip_flop_1_q[2]));  // open: CLOCK_OUT, Q_BAR
  LEVEL_TRIGGERED_D_TYPE_FLIP_FLOP level_triggered_d_type_flip_flop_4 (
    .DATA(DATA), .CLOCK(eight_bit_initializer_1_out[3]), .Q(level_triggered_d_type_flip_flop_1_q[3]));  // open: CLOCK_OUT, Q_BAR
  LEVEL_TRIGGERED_D_TYPE_FLIP_FLOP level_triggered_d_type_flip_flop_5 (
    .DATA(DATA), .CLOCK(eight_bit_initializer_1_out[4]), .Q(level_triggered_d_type_flip_flop_1_q[4]));  // open: CLOCK_OUT, Q_BAR
  LEVEL_TRIGGERED_D_TYPE_FLIP_FLOP level_triggered_d_type_flip_flop_6 (
    .DATA(DATA), .CLOCK(eight_bit_initializer_1_out[5]), .Q(level_triggered_d_type_flip_flop_1_q[5]));  // open: CLOCK_OUT, Q_BAR
  LEVEL_TRIGGERED_D_TYPE_FLIP_FLOP level_triggered_d_type_flip_flop_7 (
    .DATA(DATA), .CLOCK(eight_bit_initializer_1_out[6]), .Q(level_triggered_d_type_flip_flop_1_q[6]));  // open: CLOCK_OUT, Q_BAR
  LEVEL_TRIGGERED_D_TYPE_FLIP_FLOP level_triggered_d_type_flip_flop_8 (
    .DATA(DATA), .CLOCK(eight_bit_initializer_1_out[7]), .Q(level_triggered_d_type_flip_flop_1_q[7]));  // open: CLOCK_OUT, Q_BAR
  EIGHT_LINE_TO_ONE_SELECTOR eight_line_to_one_selector_1 (
    .DATA(level_triggered_d_type_flip_flop_1_q), .SELECTOR(ADDRESS), .OUT(OUT));
endmodule

// INIT
module EIGHT_BIT_INITIALIZER (
  input  [7:0] A,
  input  INITIALIZE,
  output INITIALIZE_OUT,
  output [7:0] OUT
);

  wire not_1_out, two_line_to_one_selector_1_select_out, two_line_to_one_selector_2_select_out,
       two_line_to_one_selector_3_select_out, two_line_to_one_selector_4_select_out,
       two_line_to_one_selector_5_select_out, two_line_to_one_selector_6_select_out,
       two_line_to_one_selector_7_select_out;

  NOT not_1 (.IN(INITIALIZE), .OUT(not_1_out));
  TWO_LINE_TO_ONE_SELECTOR two_line_to_one_selector_1 (
    .A(A[0]), .B(INITIALIZE), .SELECT(not_1_out), .SELECT_OUT(two_line_to_one_selector_1_select_out),
    .OUT(OUT[0]));
  TWO_LINE_TO_ONE_SELECTOR two_line_to_one_selector_2 (
    .A(A[1]), .B(INITIALIZE), .SELECT(two_line_to_one_selector_1_select_out),
    .SELECT_OUT(two_line_to_one_selector_2_select_out), .OUT(OUT[1]));
  TWO_LINE_TO_ONE_SELECTOR two_line_to_one_selector_3 (
    .A(A[2]), .B(INITIALIZE), .SELECT(two_line_to_one_selector_2_select_out),
    .SELECT_OUT(two_line_to_one_selector_3_select_out), .OUT(OUT[2]));
  TWO_LINE_TO_ONE_SELECTOR two_line_to_one_selector_4 (
    .A(A[3]), .B(INITIALIZE), .SELECT(two_line_to_one_selector_3_select_out),
    .SELECT_OUT(two_line_to_one_selector_4_select_out), .OUT(OUT[3]));
  TWO_LINE_TO_ONE_SELECTOR two_line_to_one_selector_5 (
    .A(A[4]), .B(INITIALIZE), .SELECT(two_line_to_one_selector_4_select_out),
    .SELECT_OUT(two_line_to_one_selector_5_select_out), .OUT(OUT[4]));
  TWO_LINE_TO_ONE_SELECTOR two_line_to_one_selector_6 (
    .A(A[5]), .B(INITIALIZE), .SELECT(two_line_to_one_selector_5_select_out),
    .SELECT_OUT(two_line_to_one_selector_6_select_out), .OUT(OUT[5]));
  TWO_LINE_TO_ONE_SELECTOR two_line_to_one_selector_7 (
    .A(A[6]), .B(INITIALIZE), .SELECT(two_line_to_one_selector_6_select_out),
    .SELECT_OUT(two_line_to_one_selector_7_select_out), .OUT(OUT[6]));
  TWO_LINE_TO_ONE_SELECTOR two_line_to_one_selector_8 (
    .A(A[7]), .B(INITIALIZE), .SELECT(two_line_to_one_selector_7_select_out), .OUT(OUT[7]));  // open: SELECT_OUT

  assign INITIALIZE_OUT = INITIALIZE;
endmodule

// RAM
module SIXTEEN_BY_ONE_RAM (
  input  DATA,
  input  [3:0] ADDRESS,
  input  INITIALIZE,
  input  WRITE,
  output INITIALIZE_OUT,
  output OUT
);

  wire eight_by_one_ram_1_out, eight_by_one_ram_2_initialize_out, eight_by_one_ram_2_out, not_1_out;
  wire [1:0] one_line_to_two_decoder_1_out;

  ONE_LINE_TO_TWO_DECODER one_line_to_two_decoder_1 (
    .DATA(DATA), .SELECT(ADDRESS[3]), .OUT(one_line_to_two_decoder_1_out));
  NOT not_1 (.IN(ADDRESS[3]), .OUT(not_1_out));
  EIGHT_BY_ONE_RAM eight_by_one_ram_1 (
    .DATA(one_line_to_two_decoder_1_out[0]), .WRITE(WRITE), .ADDRESS(ADDRESS[2:0]),
    .INITIALIZE_OUT(INITIALIZE_OUT), .INITIALIZE(eight_by_one_ram_2_initialize_out),
    .OUT(eight_by_one_ram_1_out));
  EIGHT_BY_ONE_RAM eight_by_one_ram_2 (
    .DATA(one_line_to_two_decoder_1_out[1]), .WRITE(WRITE), .ADDRESS(ADDRESS[2:0]),
    .INITIALIZE_OUT(eight_by_one_ram_2_initialize_out), .INITIALIZE(INITIALIZE), .OUT(eight_by_one_ram_2_out));
  TWO_LINE_TO_ONE_SELECTOR two_line_to_one_selector_1 (
    .A(eight_by_one_ram_1_out), .B(eight_by_one_ram_2_out), .SELECT(not_1_out), .OUT(OUT));  // open: SELECT_OUT
endmodule

// D
module ONE_LINE_TO_TWO_DECODER (
  input  DATA,
  input  SELECT,
  output [1:0] OUT
);

  wire not_1_out;

  NOT not_1 (.IN(SELECT), .OUT(not_1_out));
  AND and_1 (.A(DATA), .B(not_1_out), .OUT(OUT[0]));
  AND and_2 (.A(DATA), .B(SELECT), .OUT(OUT[1]));
endmodule
